# Fritzing sketch Fritzing (saved by Fritzing 0.9.0b)
perfboards: 1

parts:
  Part1 = Arduino Nano (Rev3.0)
  Part2 = Arduino Due (Rev2b)
  Part3 = IMU Digital Combo Board 6DOF
  LED1 = 7-SEGMENT-4DIGIT-YOUNGSUN [package=7-segment-4digit-youngsun]
  R1 = Resistor [tolerance=±5% resistance=10k package=THT]
  R2 = Resistor [tolerance=±5% resistance=4.7k package=THT]
  J1 = Piezo Speaker

nets:
  N1: Part1.D1/TX, R2.Pin_1
  N2: Part1.D4, Part3.SDA
  N3: Part1.D5, Part3.SCL, Part3.INT1
  GND: Part1.GND, Part2.GND, Part3.GND, R1.Pin_1, J1.pin1
  N4: Part2.D19/RX1, R1.Pin_0, R2.Pin_0
  N5: Part2.IOREF, Part3.3.3V
  N6: Part2.D23, J1.pin2
  N7: Part2.D31, LED1.DIG1
  N8: Part2.D33, LED1.DIG2
  N9: Part2.D35, LED1.D
  N10: Part2.D37, LED1.COL-A
  N11: Part2.D39, LED1.E
  N12: Part2.D41, LED1.DIG3
  N13: Part2.D43, LED1.B
  N14: Part2.D45, LED1.G
  N15: Part2.D47, LED1.A
  N16: Part2.D49, LED1.C
  N17: Part2.D51, LED1.COL-C
  N18: Part2.D53, LED1.F

notes:
  OrangeRX DSMX Sattelite Receiver
  ESC
